// Logisim project 74LS107.circ as structural Verilog: 1 circuit, main circuit L_74LS107_f74dca52
module L_74LS107_f74dca52 (
  input  J1,
  input  CLK1,
  input  K1,
  input  CLR1,
  input  J2,
  input  CLK2,
  input  K2,
  input  CLR2,
  output Q1,
  output NOTQ1,
  output Q2,
  output NOTQ2
);

  wire not_1_out, not_2_out;

  J_K_Flip_Flop #(.trigger("falling")) Fall (
    .J(J1), .K(K1), .clk(CLK1), .Q(Q1), .Qn(NOTQ1), .reset(not_1_out));  // open: preset
  not not_1 (not_1_out, CLR1);
  J_K_Flip_Flop #(.trigger("falling")) j_k_ff_1 (
    .J(J2), .K(K2), .clk(CLK2), .Q(Q2), .Qn(NOTQ2), .reset(not_2_out));  // open: preset
  not not_2 (not_2_out, CLR2);

  // Notes on the sheet:
  //   74LS107
endmodule
