// Logisim project 74LS126.circ as structural Verilog: 1 circuit, main circuit L_74LS126_5b2bd483
module L_74LS126_5b2bd483 (
  input  A1,
  input  G1,
  input  A2,
  input  G2,
  input  A3,
  input  G3,
  input  A4,
  input  G4,
  output Y1,
  output Y2,
  output Y3,
  output Y4
);

  assign Y1 = G1 ? A1 : 1'bz;  // Controlled_Buffer controlled_buffer_1
  assign Y2 = G2 ? A2 : 1'bz;  // Controlled_Buffer controlled_buffer_2
  assign Y3 = G3 ? A3 : 1'bz;  // Controlled_Buffer controlled_buffer_3
  assign Y4 = G4 ? A4 : 1'bz;  // Controlled_Buffer controlled_buffer_4

  // Notes on the sheet:
  //   74LS126
endmodule
