// Logisim project 74LS157.circ as structural Verilog: 1 circuit, main circuit L_74LS157_d074910b
module L_74LS157_d074910b (
  input  A1,
  input  B1,
  input  A2,
  input  B2,
  input  A3,
  input  B3,
  input  A4,
  input  B4,
  input  STROBE_G,
  input  SELECT_A_B,
  output Y1,
  output Y2,
  output Y3,
  output Y4
);

  wire and_1_out, and_2_out, and_3_out, and_4_out, and_5_out, and_6_out, and_7_out, and_8_out, and_9_out,
       and_10_out, not_1_out;

  not not_1 (not_1_out, SELECT_A_B);
  and and_1 (and_1_out, ~STROBE_G, ~SELECT_A_B);  // AND_Gate
  and and_2 (and_2_out, ~STROBE_G, ~not_1_out);  // AND_Gate
  and and_3 (and_3_out, A1, and_1_out);
  and and_4 (and_4_out, B1, and_2_out);
  and and_5 (and_5_out, A2, and_1_out);
  and and_6 (and_6_out, B2, and_2_out);
  and and_7 (and_7_out, A3, and_1_out);
  and and_8 (and_8_out, B3, and_2_out);
  and and_9 (and_9_out, A4, and_1_out);
  and and_10 (and_10_out, B4, and_2_out);
  or or_1 (Y1, and_3_out, and_4_out);
  or or_2 (Y2, and_5_out, and_6_out);
  or or_3 (Y3, and_7_out, and_8_out);
  or or_4 (Y4, and_9_out, and_10_out);

  // Notes on the sheet:
  //   74LS157
endmodule
