// Logisim project 74LS189.circ as structural Verilog: 1 circuit, main circuit L_74LS189_c76b68cd
module L_74LS189_c76b68cd (
  input  A0,
  input  A1,
  input  A2,
  input  A3,
  input  DI1,
  input  DI2,
  input  DI3,
  input  DI4,
  input  NOT_S,
  input  NOT_W,
  output NOT_DO1,
  output NOT_DO2,
  output NOT_DO3,
  output NOT_DO4
);

  wire and_1_out, CS, not_3_out, OE, W, WE;
  wire [3:0] controlled_buffer_1_out;

  not not_1 (CS, NOT_S);
  RAM #(.addrWidth(4), .dataWidth(4), .databus("bidir"), .trigger("high")) ram_1 (
    .addr({A3, A2, A1, A0}), .we(WE), .oe(OE));  // open: clk, data
  not not_2 (W, NOT_W);
  and and_1 (and_1_out, CS, NOT_W);
  not not_3 (not_3_out, and_1_out);
  and and_2 (WE, W, CS);
  and and_3 (OE, NOT_W, CS);
  assign controlled_buffer_1_out = not_3_out ? {DI4, DI3, DI2, DI1} : 4'bz;  // Controlled_Buffer controlled_buffer_1
  assign {NOT_DO4, NOT_DO3, NOT_DO2, NOT_DO1} = and_1_out ? ~controlled_buffer_1_out : 4'bz;  // Controlled_Inverter controlled_inverter_1

  // Other names for the same wires on the sheet: R = NOT_W

  // Notes on the sheet:
  //   74LS189
endmodule
