// Logisim project 74LS83.circ as structural Verilog: 1 circuit, main circuit L_74LS83_a67a6f6d
module L_74LS83_a67a6f6d (
  input  B4,
  input  A4,
  input  B3,
  input  A3,
  input  B2,
  input  A2,
  input  B1,
  input  A1,
  input  C0,
  output C4,
  output E4,
  output E3,
  output E2,
  output E1
);

  wire and_1_out, and_2_out, and_3_out, and_4_out, and_5_out, and_6_out, and_7_out, and_8_out, and_9_out,
       and_10_out, and_11_out, and_12_out, and_13_out, and_14_out, buffer_1_out, buffer_2_out, buffer_3_out,
       buffer_4_out, nand_1_out, nand_2_out, nand_3_out, nand_4_out, nor_1_out, nor_2_out, nor_3_out,
       nor_4_out, nor_6_out, nor_7_out, nor_8_out, not_1_out, not_2_out;

  nand nand_1 (nand_1_out, B4, A4);
  nor nor_1 (nor_1_out, B4, A4);
  nand nand_2 (nand_2_out, B3, A3);
  nor nor_2 (nor_2_out, B3, A3);
  nand nand_3 (nand_3_out, B2, A2);
  nor nor_3 (nor_3_out, B2, A2);
  nand nand_4 (nand_4_out, B1, A1);
  nor nor_4 (nor_4_out, B1, A1);
  not not_1 (not_1_out, C0);
  buf buffer_1 (buffer_1_out, nor_1_out);
  and and_1 (and_1_out, nor_2_out, nand_1_out);
  and and_2 (and_2_out, nor_3_out, nand_1_out, nand_2_out);
  and and_3 (and_3_out, nor_4_out, nand_1_out, nand_2_out, nand_3_out);
  and and_4 (and_4_out, nand_1_out, nand_2_out, nand_3_out, nand_4_out, not_1_out);
  and and_5 (and_5_out, nand_1_out, ~nor_1_out);  // AND_Gate
  buf buffer_2 (buffer_2_out, nor_2_out);
  and and_6 (and_6_out, nor_3_out, nand_2_out);
  and and_7 (and_7_out, nor_4_out, nand_2_out, nand_3_out);
  and and_8 (and_8_out, nand_2_out, nand_3_out, nand_4_out, not_1_out);
  and and_9 (and_9_out, nand_2_out, ~nor_2_out);  // AND_Gate
  buf buffer_3 (buffer_3_out, nor_3_out);
  and and_10 (and_10_out, nor_4_out, nand_3_out);
  and and_11 (and_11_out, nand_3_out, nand_4_out, not_1_out);
  and and_12 (and_12_out, nand_3_out, ~nor_3_out);  // AND_Gate
  buf buffer_4 (buffer_4_out, nor_4_out);
  and and_13 (and_13_out, nand_4_out, not_1_out);
  and and_14 (and_14_out, nand_4_out, ~nor_4_out);  // AND_Gate
  not not_2 (not_2_out, not_1_out);
  nor nor_5 (C4, buffer_1_out, and_1_out, and_2_out, and_3_out, and_4_out);
  nor nor_6 (nor_6_out, buffer_2_out, and_6_out, and_7_out, and_8_out);
  nor nor_7 (nor_7_out, buffer_3_out, and_10_out, and_11_out);
  nor nor_8 (nor_8_out, buffer_4_out, and_13_out);
  xor xor_1 (E4, and_5_out, nor_6_out);
  xor xor_2 (E3, and_9_out, nor_7_out);
  xor xor_3 (E2, and_12_out, nor_8_out);
  xor xor_4 (E1, and_14_out, not_2_out);

  // Notes on the sheet:
  //   74LS83
  //   74LS83
endmodule
