// Logisim project sap1_1.circ as structural Verilog: 1 circuit, main circuit main
module main (
);

  wire A_sw1, A_sw2, A_sw3, A_sw4, and_1_out, AUTO_CLK_out, C1_q1, C1_q2, C2_q1, C2_q2, C4_g4, C4_q1, C4_q2,
       C4_q3, C5_y1, C5_y2, C5_y3, C5_y4, C6_not_do1, C6_not_do2, C6_not_do3, C6_not_do4, C7_not_do1,
       C7_not_do2, C7_not_do3, C7_not_do4, C10_g4, C10_q1, C10_q2, C10_q3, C11_g4, C11_q1, C11_q2, C11_q3,
       C14_pin1, C14_pin3, C14_pin4, C14_pin6, C14_pin8, C14_pin9, C14_pin11, C14_pin12, C15_pin3, C15_pin6,
       C15_pin8, C15_pin11, C16_e1, C16_e2, C16_e3, C16_e4, C17_c4, C17_e1, C17_e2, C17_e3, C17_e4, C20_g4,
       C20_q1, C20_q2, C20_q3, C22_g4, C22_q1, C22_q2, C22_q3, C23_g4, C23_q1, C23_q2, C23_q3, C24_pin9,
       C24_pin11, C24_pin12, C26_pin2, C26_pin3, C26_pin11, C26_pin12, C26_pin13, C27_pin2, C31_pin1,
       C31_pin2, C31_pin3, C31_pin4, C31_pin5, C31_pin6, C31_pin8, C31_pin9, C35_pin1, C35_pin2, C35_pin3,
       C35_pin4, C35_pin5, C35_pin6, C35_pin8, C35_pin9, C35_pin10, C35_pin12, C36_notq1, C36_notq2,
       C37_notq1, C37_notq2, C38_notq2, C38_q1, C39_pin3, C39_pin6, C39_pin8, C39_pin11, C40_pin3, C40_pin6,
       C40_pin8, C40_pin11, C41_pin3, C41_pin6, C41_pin8, C41_pin11, C42_pin3, C42_pin6, C42_pin8, C42_pin11,
       C43_pin3, C43_pin6, C44_pin6, C44_pin8, C45_pin6, C45_pin12, C46_pin6, CLK, CLR, Cp, dipswitch_1_sw1,
       dipswitch_1_sw2, dipswitch_1_sw3, dipswitch_1_sw4, dipswitch_1_sw5, dipswitch_1_sw6, dipswitch_1_sw7,
       dipswitch_1_sw8, EA, Ep, Eu, not_1_out, not_2_out, NOT_CE, NOT_CLK, NOT_CLR, NOT_E1, NOT_HLT, NOT_L0,
       NOT_L1, NOT_LA, NOT_LB, NOT_Lm, READ_WRITE_out, RUN_PROG_sw1, S2_sw1, S7_sw1, Su, T3, T4, T5, T6;

  DipSwitch dipswitch_1 (
    .sw1(dipswitch_1_sw1), .sw2(dipswitch_1_sw2), .sw3(dipswitch_1_sw3), .sw4(dipswitch_1_sw4),
    .sw5(dipswitch_1_sw5), .sw6(dipswitch_1_sw6), .sw7(dipswitch_1_sw7), .sw8(dipswitch_1_sw8));
  DipSwitch #(.number(1)) RUN_PROG (.sw1(RUN_PROG_sw1));
  L_74LS107_f74dca52 C38 (
    .CLK1(CLK), .K1(T6), .CLR1(NOT_CLR), .J2(Ep), .CLK2(CLK), .K2(C38_q1), .CLR2(NOT_CLR), .J1(C36_notq2),
    .Q1(C38_q1), .NOTQ1(Ep), .Q2(Cp), .NOTQ2(C38_notq2));
  L_74LS107_f74dca52 C37 (
    .CLK1(CLK), .K1(C38_notq2), .CLR1(NOT_CLR), .J2(T3), .CLK2(CLK), .K2(C37_notq1), .CLR2(NOT_CLR), .J1(Cp),
    .Q1(T3), .NOTQ1(C37_notq1), .Q2(T4), .NOTQ2(C37_notq2));
  L_74LS107_f74dca52 C36 (
    .CLK1(CLK), .K1(C37_notq2), .CLR1(NOT_CLR), .J2(T5), .CLK2(CLK), .K2(C36_notq1), .CLR2(NOT_CLR), .J1(T4),
    .Q1(T5), .NOTQ1(C36_notq1), .Q2(T6), .NOTQ2(C36_notq2));
  DipSwitch #(.number(4)) A (.sw1(A_sw1), .sw2(A_sw2), .sw3(A_sw3), .sw4(A_sw4));
  and and_1 (and_1_out, NOT_CE, RUN_PROG_sw1);
  _7404 #(.ShowInternalStructure("true")) C35 (
    .pin1(C35_pin1), .pin2(C35_pin2), .pin3(C35_pin3), .pin4(C35_pin4), .pin5(C35_pin5), .pin6(C35_pin6),
    .pin13(T3), .pin12(C35_pin12), .pin11(Ep), .pin10(C35_pin10), .pin9(C35_pin9), .pin8(C35_pin8));
  Button #(.press("passive")) READ_WRITE (.out(READ_WRITE_out));
  _7400 #(.ShowInternalStructure("true")) C43 (
    .pin1(C35_pin4), .pin2(T5), .pin3(C43_pin3), .pin4(C35_pin6), .pin5(T5), .pin6(C43_pin6), .pin10(T4),
    .pin9(C35_pin8), .pin8(NOT_L0));  // open: pin13, pin12, pin11
  _7400 #(.ShowInternalStructure("true")) C42 (
    .pin1(C35_pin8), .pin2(T4), .pin3(C42_pin3), .pin4(C35_pin6), .pin5(T6), .pin6(C42_pin6), .pin13(T6),
    .pin12(C35_pin6), .pin11(C42_pin11), .pin10(T6), .pin9(C35_pin4), .pin8(C42_pin8));
  _7400 #(.ShowInternalStructure("true")) C41 (
    .pin1(C35_pin6), .pin2(T4), .pin3(C41_pin3), .pin4(C35_pin2), .pin5(T5), .pin6(C41_pin6), .pin13(T6),
    .pin12(C35_pin6), .pin11(C41_pin11), .pin10(T6), .pin9(C35_pin4), .pin8(C41_pin8));
  _7400 #(.ShowInternalStructure("true")) C40 (
    .pin1(C35_pin4), .pin2(T5), .pin3(C40_pin3), .pin4(C35_pin6), .pin5(T5), .pin6(C40_pin6), .pin13(T4),
    .pin12(C35_pin4), .pin11(C40_pin11), .pin10(T4), .pin9(C35_pin2), .pin8(C40_pin8));
  _7400 #(.ShowInternalStructure("true")) C39 (
    .pin1(C35_pin2), .pin2(T4), .pin3(C39_pin3), .pin4(C35_pin4), .pin5(T4), .pin6(C39_pin6), .pin13(T5),
    .pin12(C35_pin2), .pin11(C39_pin11), .pin10(T4), .pin9(C35_pin6), .pin8(C39_pin8));
  L_74LS107_f74dca52 C2 (
    .CLK1(NOT_CLK), .K1(Cp), .CLR1(NOT_CLR), .J2(Cp), .CLK2(C2_q1), .K2(Cp), .CLR2(NOT_CLR), .J1(Cp),
    .Q1(C2_q1), .Q2(C2_q2));  // open: NOTQ1, NOTQ2
  L_74LS107_f74dca52 C1 (
    .CLK1(C2_q2), .K1(Cp), .CLR1(NOT_CLR), .J2(Cp), .CLK2(C1_q1), .K2(Cp), .CLR2(NOT_CLR), .J1(Cp),
    .Q1(C1_q1), .Q2(C1_q2));  // open: NOTQ1, NOTQ2
  _7404 #(.ShowInternalStructure("true")) C31 (
    .pin1(C31_pin1), .pin2(C31_pin2), .pin3(C31_pin3), .pin4(C31_pin4), .pin5(C31_pin5), .pin6(C31_pin6),
    .pin9(C31_pin9), .pin8(C31_pin8));  // open: pin13, pin12, pin11, pin10
  _7420 #(.ShowInternalStructure("true")) C32 (
    .pin1(C31_pin2), .pin2(C31_pin4), .pin4(C31_pin6), .pin5(C31_pin8), .pin6(C35_pin1), .pin13(C31_pin9),
    .pin12(C31_pin6), .pin10(C31_pin4), .pin9(C31_pin2), .pin8(C35_pin3));  // open: pin3, pin11
  _7420 #(.ShowInternalStructure("true")) C33 (
    .pin1(C31_pin2), .pin2(C31_pin4), .pin4(C31_pin5), .pin5(C31_pin8), .pin6(C35_pin5), .pin13(C31_pin8),
    .pin12(C31_pin5), .pin10(C31_pin3), .pin9(C31_pin1), .pin8(C35_pin9));  // open: pin3, pin11
  _7420 #(.ShowInternalStructure("true")) C34 (
    .pin1(C31_pin1), .pin2(C31_pin3), .pin4(C31_pin5), .pin5(C31_pin9), .pin6(NOT_HLT));  // open: pin3, pin13, pin12, pin11, pin10, pin9, pin8
  L_74LS173_6bdbcc89 C4 (
    .N(1'b0), .D1(C7_not_do1), .NOT_G1(NOT_Lm), .NOT_G2(NOT_Lm), .D2(C7_not_do2), .CLK(CLK), .D3(C7_not_do3),
    .D4(C7_not_do4), .CLR(1'b0), .M(1'b0), .Q1(C4_q1), .Q2(C4_q2), .Q3(C4_q3), .G4(C4_g4));
  L_74LS157_d074910b C5 (
    .B1(C4_g4), .A2(A_sw2), .B2(C4_q3), .A3(A_sw3), .B3(C4_q2), .A4(A_sw4), .B4(C4_q1), .STROBE_G(1'b0),
    .SELECT_A_B(S2_sw1), .A1(A_sw1), .Y1(C5_y1), .Y2(C5_y2), .Y3(C5_y3), .Y4(C5_y4));
  DipSwitch #(.number(1)) S2 (.sw1(S2_sw1));
  L_74LS189_c76b68cd C7 (
    .A0(C5_y4), .A1(C5_y3), .A2(C5_y2), .A3(C5_y1), .DI1(dipswitch_1_sw4), .DI2(dipswitch_1_sw3),
    .DI3(dipswitch_1_sw2), .DI4(dipswitch_1_sw1), .NOT_S(and_1_out), .NOT_W(READ_WRITE_out),
    .NOT_DO2(C7_not_do2), .NOT_DO3(C7_not_do3), .NOT_DO4(C7_not_do4), .NOT_DO1(C7_not_do1));
  L_74LS189_c76b68cd C6 (
    .A0(C5_y4), .A1(C5_y3), .A2(C5_y2), .A3(C5_y1), .DI1(dipswitch_1_sw8), .DI2(dipswitch_1_sw7),
    .DI3(dipswitch_1_sw6), .DI4(dipswitch_1_sw5), .NOT_S(and_1_out), .NOT_W(READ_WRITE_out),
    .NOT_DO2(C6_not_do2), .NOT_DO3(C6_not_do3), .NOT_DO4(C6_not_do4), .NOT_DO1(C6_not_do1));
  L_74LS173_6bdbcc89 C9 (
    .N(NOT_E1), .D1(C7_not_do1), .NOT_G1(NOT_L1), .NOT_G2(NOT_L1), .D2(C7_not_do2), .CLK(CLK),
    .D3(C7_not_do3), .D4(C7_not_do4), .CLR(1'b0), .M(NOT_E1), .Q1(C7_not_do1), .Q2(C7_not_do2),
    .Q3(C7_not_do3), .G4(C7_not_do4));
  L_74LS173_6bdbcc89 C8 (
    .N(1'b0), .D1(C6_not_do1), .NOT_G1(NOT_L1), .NOT_G2(NOT_L1), .D2(C6_not_do2), .CLK(CLK), .D3(C6_not_do3),
    .D4(C6_not_do4), .CLR(CLR), .M(1'b0), .Q1(C31_pin1), .Q2(C31_pin3), .Q3(C31_pin5), .G4(C31_pin9));
  L_74LS126_5b2bd483 C3 (
    .A1(C1_q1), .G1(Ep), .A2(C1_q2), .G2(Ep), .A3(C2_q1), .G3(Ep), .A4(C2_q2), .G4(Ep), .Y1(C7_not_do1),
    .Y2(C7_not_do2), .Y3(C7_not_do3), .Y4(C7_not_do4));
  _7400 #(.ShowInternalStructure("true")) C46 (
    .pin1(C42_pin8), .pin2(C42_pin11), .pin3(Eu), .pin4(C43_pin3), .pin5(C43_pin6), .pin6(C46_pin6));  // open: pin13, pin12, pin11, pin10, pin9, pin8
  _7410 #(.ShowInternalStructure("true")) C45 (
    .pin1(C40_pin8), .pin2(C40_pin11), .pin3(C41_pin6), .pin4(C41_pin8), .pin5(C41_pin11), .pin6(C45_pin6),
    .pin13(C41_pin3), .pin12(C45_pin12));  // open: pin11, pin10, pin9, pin8
  _7420 #(.ShowInternalStructure("true")) C44 (
    .pin1(C35_pin10), .pin2(C39_pin3), .pin4(C39_pin6), .pin5(C39_pin8), .pin6(C44_pin6), .pin13(C40_pin6),
    .pin12(C40_pin3), .pin10(C39_pin11), .pin9(C35_pin12), .pin8(C44_pin8));  // open: pin3, pin11
  _7404 #(.ShowInternalStructure("true")) C48 (
    .pin1(C42_pin6), .pin2(Su), .pin3(C46_pin6), .pin4(NOT_LB));  // open: pin5, pin6, pin13, pin12, pin11, pin10, pin9, pin8
  _7404 #(.ShowInternalStructure("true")) C47 (
    .pin1(C44_pin6), .pin2(NOT_Lm), .pin3(C44_pin8), .pin4(NOT_CE), .pin5(T3), .pin6(NOT_L1),
    .pin13(C42_pin3), .pin12(EA), .pin11(C45_pin6), .pin10(NOT_LA), .pin9(C45_pin12), .pin8(NOT_E1));
  // Probe on C6_not_do1
  // Probe on C6_not_do2
  // Probe on C7_not_do1
  // Probe on C7_not_do2
  // Probe on C4_q1
  // Probe on C4_q2
  // Probe on C7_not_do1
  // Probe on C7_not_do2
  // Probe on C31_pin1
  // Probe on C31_pin3
  // Probe on C6_not_do3
  // Probe on C6_not_do4
  // Probe on C7_not_do1
  // Probe on C7_not_do3
  // Probe on C7_not_do4
  // Probe on C4_q3
  // Probe on C4_g4
  // Probe on C7_not_do3
  // Probe on C7_not_do4
  // Probe on C31_pin5
  // Probe on C31_pin9
  // Probe on C7_not_do2
  // Probe on C7_not_do3
  // Probe on C7_not_do4
  L_74LS173_6bdbcc89 C11 (
    .N(1'b0), .D1(C7_not_do1), .NOT_G1(NOT_LA), .NOT_G2(NOT_LA), .D2(C7_not_do2), .CLK(CLK), .D3(C7_not_do3),
    .D4(C7_not_do4), .M(1'b0), .Q1(C11_q1), .Q2(C11_q2), .Q3(C11_q3), .G4(C11_g4));  // open: CLR
  L_74LS173_6bdbcc89 C10 (
    .N(1'b0), .D1(C6_not_do1), .NOT_G1(NOT_LA), .NOT_G2(NOT_LA), .D2(C6_not_do2), .CLK(CLK), .D3(C6_not_do3),
    .D4(C6_not_do4), .M(1'b0), .Q1(C10_q1), .Q2(C10_q2), .Q3(C10_q3), .G4(C10_g4));  // open: CLR
  L_74LS83_a67a6f6d C16 (
    .B4(C14_pin3), .A4(C10_q1), .B3(C14_pin6), .A3(C10_q2), .B2(C14_pin8), .A2(C10_q3), .B1(C14_pin11),
    .A1(C10_g4), .C0(C17_c4), .E4(C16_e4), .E3(C16_e3), .E2(C16_e2), .E1(C16_e1));  // open: C4
  _7486 #(.ShowInternalStructure("true")) C14 (
    .pin1(C14_pin1), .pin2(Su), .pin3(C14_pin3), .pin4(C14_pin4), .pin5(Su), .pin6(C14_pin6), .pin13(Su),
    .pin12(C14_pin12), .pin11(C14_pin11), .pin10(Su), .pin9(C14_pin9), .pin8(C14_pin8));
  // Probe on Cp
  // Probe on Ep
  // Probe on NOT_Lm
  // Probe on NOT_CE
  // Probe on NOT_L1
  // Probe on NOT_E1
  // Probe on NOT_LA
  // Probe on EA
  // Probe on Su
  // Probe on Eu
  // Probe on NOT_LB
  // Probe on NOT_L0
  L_74LS126_5b2bd483 C18 (
    .A1(C16_e4), .G1(Eu), .A2(C16_e3), .G2(Eu), .A3(C16_e2), .G3(Eu), .A4(C16_e1), .G4(Eu), .Y1(C6_not_do1),
    .Y2(C6_not_do2), .Y3(C6_not_do3), .Y4(C6_not_do4));
  L_74LS173_6bdbcc89 C21 (
    .N(1'b0), .D1(C7_not_do1), .NOT_G1(NOT_LB), .NOT_G2(NOT_LB), .D2(C7_not_do2), .CLK(CLK), .D3(C7_not_do3),
    .D4(C7_not_do4), .M(1'b0), .Q1(C14_pin12), .Q2(C14_pin9), .Q3(C14_pin4), .G4(C14_pin1));  // open: CLR
  L_74LS173_6bdbcc89 C20 (
    .N(1'b0), .D1(C6_not_do1), .NOT_G1(NOT_LB), .NOT_G2(NOT_LB), .D2(C6_not_do2), .CLK(CLK), .D3(C6_not_do3),
    .D4(C6_not_do4), .M(1'b0), .Q1(C20_q1), .Q2(C20_q2), .Q3(C20_q3), .G4(C20_g4));  // open: CLR
  L_74LS173_6bdbcc89 C23 (
    .N(1'b0), .D1(C7_not_do1), .NOT_G1(NOT_L0), .NOT_G2(NOT_L0), .D2(C7_not_do2), .CLK(CLK), .D3(C7_not_do3),
    .D4(C7_not_do4), .M(1'b0), .Q1(C23_q1), .Q2(C23_q2), .Q3(C23_q3), .G4(C23_g4));  // open: CLR
  L_74LS173_6bdbcc89 C22 (
    .N(1'b0), .D1(C6_not_do1), .NOT_G1(NOT_L0), .NOT_G2(NOT_L0), .D2(C6_not_do2), .CLK(CLK), .D3(C6_not_do3),
    .D4(C6_not_do4), .M(1'b0), .Q1(C22_q1), .Q2(C22_q2), .Q3(C22_q3), .G4(C22_g4));  // open: CLR
  L_74LS126_5b2bd483 C12 (
    .A1(C11_g4), .G1(EA), .A2(C11_q3), .G2(EA), .A3(C11_q2), .G3(EA), .A4(C11_q1), .G4(EA), .Y1(C7_not_do4),
    .Y2(C7_not_do3), .Y3(C7_not_do2), .Y4(C7_not_do1));
  L_74LS126_5b2bd483 C13 (
    .A1(C10_g4), .G1(EA), .A2(C10_g4), .G2(EA), .A3(C10_g4), .G3(EA), .A4(C10_g4), .G4(EA), .Y1(C6_not_do4),
    .Y2(C6_not_do3), .Y3(C6_not_do2), .Y4(C6_not_do1));
  L_74LS83_a67a6f6d C17 (
    .B4(C15_pin3), .A4(C11_q1), .B3(C15_pin6), .A3(C11_q2), .B2(C15_pin8), .A2(C11_q3), .B1(C15_pin11),
    .A1(C11_g4), .C0(Su), .C4(C17_c4), .E4(C17_e4), .E3(C17_e3), .E2(C17_e2), .E1(C17_e1));
  LedBar ledbar_1 (
    .led0(C22_q1), .led1(C22_q2), .led2(C22_q3), .led3(C22_g4), .led4(C23_q1), .led5(C23_q2), .led6(C23_q3),
    .led7(C23_g4));
  // Probe on C6_not_do1
  // Probe on C6_not_do2
  _7486 #(.ShowInternalStructure("true")) C15 (
    .pin1(C20_q1), .pin2(Su), .pin3(C15_pin3), .pin4(C20_q2), .pin5(Su), .pin6(C15_pin6), .pin13(Su),
    .pin12(C20_g4), .pin11(C15_pin11), .pin10(Su), .pin9(C20_q3), .pin8(C15_pin8));
  DipSwitch #(.number(1)) S7 (.sw1(S7_sw1));
  // Probe on Ep
  // Probe on C6_not_do3
  // Probe on C6_not_do4
  L_74LS126_5b2bd483 C19 (
    .A1(C17_e4), .G1(Eu), .A2(C17_e3), .G2(Eu), .A3(C17_e2), .G3(Eu), .A4(C17_e1), .G4(Eu), .Y1(C7_not_do1),
    .Y2(C7_not_do2), .Y3(C7_not_do3), .Y4(C7_not_do4));
  // Probe on Cp
  // Probe on C7_not_do1
  // Probe on C7_not_do2
  // Probe on C7_not_do3
  not not_1 (not_1_out, C24_pin9);
  Clock AUTO_CLK (.out(AUTO_CLK_out));
  // Probe on T3
  // Probe on C7_not_do4
  // Probe on C20_q1
  // Probe on C20_q2
  _7400 #(.ShowInternalStructure("true")) C24 (
    .pin13(not_1_out), .pin12(C24_pin12), .pin11(C24_pin11), .pin10(C24_pin11), .pin9(C24_pin9),
    .pin8(C24_pin12));  // open: pin1, pin2, pin3, pin4, pin5, pin6
  not not_2 (not_2_out, S7_sw1);
  // Probe on T4
  // Probe on T5
  // Probe on C20_q3
  // Probe on C20_g4
  // Probe on C14_pin12
  Button #(.press("passive")) S5 (.out(NOT_CLR));
  _7400 #(.ShowInternalStructure("true")) C26 (
    .pin1(S7_sw1), .pin2(C26_pin2), .pin3(C26_pin3), .pin4(C26_pin3), .pin5(not_2_out), .pin6(C26_pin2),
    .pin13(C26_pin13), .pin12(C26_pin12), .pin11(C26_pin11), .pin10(AUTO_CLK_out), .pin9(C26_pin2),
    .pin8(C26_pin13));
  // Probe on T6
  // Probe on C14_pin9
  // Probe on C14_pin4
  not not_3 (CLR, NOT_CLR);
  // Probe on C14_pin1
  nand nand_1 (C26_pin12, NOT_HLT, C24_pin11, C26_pin3);
  _7404 #(.ShowInternalStructure("true")) C27 (
    .pin1(C26_pin11), .pin2(C27_pin2), .pin3(C27_pin2), .pin4(CLK), .pin5(C26_pin11), .pin6(NOT_CLK));  // open: pin13, pin12, pin11, pin10, pin9, pin8
  Button #(.press("passive")) button_1 (.out(C24_pin9));

  // Other names for the same wires on the sheet: T1 = Ep; T2 = Cp

  // Notes on the sheet:
  //   S2
  //   Instruction Register
  //   T1
  //   T2
  //   T3
  //   T4
  //   T5
  //   T6
  //   RAM
  //   S4
  //   Program Counter
  //   MAR
  //   2 to 1 Multiplexer
  //   PC
  //   MAR
  //   IR C9 output
  //   IR I7I6I5I4
  //   Bus
  //   Accumulator
  //   B Register
  //   Output Register
  //   Adder_Subtractor
  //   Accumulator
  //   B
endmodule
